// Logisim project HERA_microprocessor.circ as structural Verilog: 22 circuits, main circuit main
module main (
);

  wire branch, CLK, not_1_out, not_2_out, write_flags, write_memory;
  wire [3:0] read_register_1, read_register_2, write_register;
  wire [4:0] flags_in, flags_out;
  wire [15:0] instruction, memory_access_address, memory_read_value, PC_in, PC_out, register_read_value_1,
       register_read_value_2, write_value;

  Clock clock_1 (.out(CLK));
  not not_1 (not_1_out, branch);
  Counter #(.width(16), .max('hffff)) counter_1 (
    .load(branch), .D(PC_out), .count(not_1_out), .Q(PC_in), .clk(CLK));  // open: carry, clr
  Hex_Digit_Display hex_digit_display_1 (.value(instruction[15:12]));  // open: dp
  Hex_Digit_Display hex_digit_display_2 (.value(PC_in[15:12]));  // open: dp
  Hex_Digit_Display hex_digit_display_3 (.value(PC_in[11:8]));  // open: dp
  Hex_Digit_Display hex_digit_display_4 (.value(instruction[11:8]));  // open: dp
  Hex_Digit_Display hex_digit_display_5 (.value(PC_in[7:4]));  // open: dp
  Hex_Digit_Display hex_digit_display_6 (.value(PC_in[3:0]));  // open: dp
  Hex_Digit_Display hex_digit_display_7 (.value(instruction[3:0]));  // open: dp
  Hex_Digit_Display hex_digit_display_8 (.value(instruction[7:4]));  // open: dp
  Hex_Digit_Display hex_digit_display_9 (.value(register_read_value_1[15:12]));  // open: dp
  ROM #(.addrWidth(16), .dataWidth(16)) rom_1 (.addr(PC_in), .data(instruction));  // open: sel
  Hex_Digit_Display hex_digit_display_10 (.value(register_read_value_1[11:8]));  // open: dp
  flags flags (
    .CLK(CLK), .sign_in(flags_out[0]), .zero_in(flags_out[1]), .overflow_in(flags_out[2]),
    .carry_in(flags_out[3]), .carry_block_in(flags_out[4]), .Write(write_flags), .sign_out(flags_in[0]),
    .zero_out(flags_in[1]), .overflow_out(flags_in[2]), .carry_out(flags_in[3]), .carry_block_out(flags_in[4]));
  Hex_Digit_Display hex_digit_display_11 (.value(read_register_1));  // open: dp
  Hex_Digit_Display hex_digit_display_12 (.value(register_read_value_1[3:0]));  // open: dp
  Hex_Digit_Display hex_digit_display_13 (.value(register_read_value_1[7:4]));  // open: dp
  LED sign (.in(flags_in[0]));
  LED zero (.in(flags_in[1]));
  LED overflow (.in(flags_in[2]));
  LED carry (.in(flags_in[3]));
  LED carry_block (.in(flags_in[4]));
  Hex_Digit_Display hex_digit_display_14 (.value(register_read_value_2[15:12]));  // open: dp
  Hex_Digit_Display hex_digit_display_15 (.value(register_read_value_2[7:4]));  // open: dp
  Hex_Digit_Display hex_digit_display_16 (.value(register_read_value_2[11:8]));  // open: dp
  ALSU ALSU (
    .Instruction(instruction), .flags_in(flags_in), .register_read_value_1(register_read_value_1),
    .register_read_value_2(register_read_value_2), .memory_read_value(memory_read_value),
    .program_counter_in(PC_in), .write_flags(write_flags), .flags_out(flags_out),
    .read_register_1(read_register_1), .read_register_2(read_register_2), .write_register(write_register),
    .write_value(write_value), .memory_access_address(memory_access_address), .write_memory(write_memory),
    .program_counter_out(PC_out), .branch(branch));
  Hex_Digit_Display hex_digit_display_17 (.value(read_register_2));  // open: dp
  Hex_Digit_Display hex_digit_display_18 (.value(register_read_value_2[3:0]));  // open: dp
  LED sign_2 (.in(flags_out[0]));
  LED zero_2 (.in(flags_out[1]));
  LED overflow_2 (.in(flags_out[2]));
  LED carry_2 (.in(flags_out[3]));
  LED carry_block_2 (.in(flags_out[4]));
  Hex_Digit_Display hex_digit_display_19 (.value(write_value[15:12]));  // open: dp
  register_bank register_bank (
    .read_address_1(read_register_1), .read_address_2(read_register_2), .write_address(write_register),
    .write_data(write_value), .CLK(CLK), .read_data_1(register_read_value_1),
    .read_data_2(register_read_value_2));
  Hex_Digit_Display hex_digit_display_20 (.value(write_value[7:4]));  // open: dp
  Hex_Digit_Display hex_digit_display_21 (.value(write_value[11:8]));  // open: dp
  LED led_1 (.in(write_flags));
  Hex_Digit_Display hex_digit_display_22 (.value(write_register));  // open: dp
  Hex_Digit_Display hex_digit_display_23 (.value(write_value[3:0]));  // open: dp
  not not_2 (not_2_out, write_memory);
  RAM #(.addrWidth(16), .dataWidth(16), .bus("separate")) ram_1 (
    .addr(memory_access_address), .din(write_value), .data(memory_read_value), .clk(CLK), .ld(not_2_out));  // open: str, sel, clr

  // Notes on the sheet:
  //   current instruction
  //   program counter
  //   contents of rom_1 (hex, n*v repeats v):
  //   3160 e188 f113 3351 e2c8 f200 3152 b431 130b e101 f100
endmodule

module register_bank (
  input  [3:0] read_address_1,
  input  [3:0] read_address_2,
  input  [3:0] write_address,
  input  [15:0] write_data,
  input  CLK,
  output [15:0] read_data_1,
  output [15:0] read_data_2
);

  wire decoder_1_out1, decoder_1_out2, decoder_1_out3, decoder_1_out4, decoder_1_out5, decoder_1_out6,
       decoder_1_out7, decoder_1_out8, decoder_1_out9, decoder_1_out10, decoder_1_out11, decoder_1_out12,
       decoder_1_out13, decoder_1_out14, decoder_1_out15;
  wire [15:0] demultiplexer_1_out0, demultiplexer_1_out1, demultiplexer_1_out2, demultiplexer_1_out3,
       demultiplexer_1_out4, demultiplexer_1_out5, demultiplexer_1_out6, demultiplexer_1_out7,
       demultiplexer_1_out8, demultiplexer_1_out9, demultiplexer_1_out10, demultiplexer_1_out11,
       demultiplexer_1_out12, demultiplexer_1_out13, demultiplexer_1_out14, demultiplexer_1_out15,
       register_1_q, register_2_q, register_3_q, register_4_q, register_5_q, register_6_q, register_7_q,
       register_8_q, register_9_q, register_10_q, register_11_q, register_12_q, register_13_q, register_14_q,
       register_15_q, register_16_q;

  Demultiplexer #(.select(4), .width(16)) demultiplexer_1 (
    .out0(demultiplexer_1_out0), .out1(demultiplexer_1_out1), .out2(demultiplexer_1_out2),
    .out3(demultiplexer_1_out3), .out4(demultiplexer_1_out4), .out5(demultiplexer_1_out5),
    .out6(demultiplexer_1_out6), .out7(demultiplexer_1_out7), .out8(demultiplexer_1_out8),
    .out9(demultiplexer_1_out9), .out10(demultiplexer_1_out10), .out11(demultiplexer_1_out11),
    .out12(demultiplexer_1_out12), .out13(demultiplexer_1_out13), .out14(demultiplexer_1_out14),
    .out15(demultiplexer_1_out15), .in(write_data), .sel(write_address));  // open: en
  Decoder #(.select(4)) decoder_1 (
    .out1(decoder_1_out1), .out2(decoder_1_out2), .out3(decoder_1_out3), .out4(decoder_1_out4),
    .out5(decoder_1_out5), .out6(decoder_1_out6), .out7(decoder_1_out7), .out8(decoder_1_out8),
    .out9(decoder_1_out9), .out10(decoder_1_out10), .out11(decoder_1_out11), .out12(decoder_1_out12),
    .out13(decoder_1_out13), .out14(decoder_1_out14), .out15(decoder_1_out15), .sel(write_address));  // open: out0, en
  Register #(.width(16)) register_1 (.D(demultiplexer_1_out0), .en(1'b0), .Q(register_1_q), .clk(CLK));  // open: clr
  Register #(.width(16)) register_2 (
    .D(demultiplexer_1_out1), .en(decoder_1_out1), .Q(register_2_q), .clk(CLK));  // open: clr
  Register #(.width(16)) register_3 (
    .D(demultiplexer_1_out2), .en(decoder_1_out2), .Q(register_3_q), .clk(CLK));  // open: clr
  Register #(.width(16)) register_4 (
    .D(demultiplexer_1_out3), .en(decoder_1_out3), .Q(register_4_q), .clk(CLK));  // open: clr
  Register #(.width(16)) register_5 (
    .D(demultiplexer_1_out4), .en(decoder_1_out4), .Q(register_5_q), .clk(CLK));  // open: clr
  Register #(.width(16)) register_6 (
    .D(demultiplexer_1_out5), .en(decoder_1_out5), .Q(register_6_q), .clk(CLK));  // open: clr
  Register #(.width(16)) register_7 (
    .D(demultiplexer_1_out6), .en(decoder_1_out6), .Q(register_7_q), .clk(CLK));  // open: clr
  Register #(.width(16)) register_8 (
    .D(demultiplexer_1_out7), .en(decoder_1_out7), .Q(register_8_q), .clk(CLK));  // open: clr
  Register #(.width(16)) register_9 (
    .D(demultiplexer_1_out8), .en(decoder_1_out8), .Q(register_9_q), .clk(CLK));  // open: clr
  Register #(.width(16)) register_10 (
    .D(demultiplexer_1_out9), .en(decoder_1_out9), .Q(register_10_q), .clk(CLK));  // open: clr
  Register #(.width(16)) register_11 (
    .D(demultiplexer_1_out10), .en(decoder_1_out10), .Q(register_11_q), .clk(CLK));  // open: clr
  Register #(.width(16)) register_12 (
    .D(demultiplexer_1_out11), .en(decoder_1_out11), .Q(register_12_q), .clk(CLK));  // open: clr
  Register #(.width(16)) register_13 (
    .D(demultiplexer_1_out12), .en(decoder_1_out12), .Q(register_13_q), .clk(CLK));  // open: clr
  Register #(.width(16)) register_14 (
    .D(demultiplexer_1_out13), .en(decoder_1_out13), .Q(register_14_q), .clk(CLK));  // open: clr
  Register #(.width(16)) register_15 (
    .D(demultiplexer_1_out14), .en(decoder_1_out14), .Q(register_15_q), .clk(CLK));  // open: clr
  Register #(.width(16)) register_16 (
    .D(demultiplexer_1_out15), .en(decoder_1_out15), .Q(register_16_q), .clk(CLK));  // open: clr
  Multiplexer #(.select(4), .width(16)) multiplexer_1 (
    .in0(register_1_q), .in1(register_2_q), .in2(register_3_q), .in3(register_4_q), .in4(register_5_q),
    .in5(register_6_q), .in6(register_7_q), .in7(register_8_q), .in8(register_9_q), .in9(register_10_q),
    .in10(register_11_q), .in11(register_12_q), .in12(register_13_q), .in13(register_14_q),
    .in14(register_15_q), .in15(register_16_q), .out(read_data_2), .sel(read_address_2));  // open: en
  Multiplexer #(.select(4), .width(16)) multiplexer_2 (
    .in0(register_1_q), .in1(register_2_q), .in2(register_3_q), .in3(register_4_q), .in4(register_5_q),
    .in5(register_6_q), .in6(register_7_q), .in7(register_8_q), .in8(register_9_q), .in9(register_10_q),
    .in10(register_11_q), .in11(register_12_q), .in12(register_13_q), .in13(register_14_q),
    .in14(register_15_q), .in15(register_16_q), .out(read_data_1), .sel(read_address_1));  // open: en
endmodule

module flags (
  input  CLK,
  input  sign_in,
  input  zero_in,
  input  overflow_in,
  input  carry_in,
  input  carry_block_in,
  input  Write,
  output sign_out,
  output zero_out,
  output overflow_out,
  output carry_out,
  output carry_block_out
);

  D_Flip_Flop d_ff_1 (.clk(CLK), .D(sign_in), .Q(sign_out), .en(Write));  // open: Qn, preset, reset
  D_Flip_Flop d_ff_2 (.clk(CLK), .D(zero_in), .Q(zero_out), .en(Write));  // open: Qn, preset, reset
  D_Flip_Flop d_ff_3 (.clk(CLK), .D(overflow_in), .Q(overflow_out), .en(Write));  // open: Qn, preset, reset
  D_Flip_Flop d_ff_4 (.clk(CLK), .D(carry_in), .Q(carry_out), .en(Write));  // open: Qn, preset, reset
  D_Flip_Flop d_ff_5 (.clk(CLK), .D(carry_block_in), .Q(carry_block_out), .en(Write));  // open: Qn, preset, reset
endmodule

module ALSU (
  input  [15:0] Instruction,
  input  [4:0] flags_in,
  input  [15:0] register_read_value_1,
  input  [15:0] register_read_value_2,
  input  [15:0] memory_read_value,
  input  [15:0] program_counter_in,
  output write_flags,
  output [4:0] flags_out,
  output [3:0] read_register_1,
  output [3:0] read_register_2,
  output [3:0] write_register,
  output [15:0] write_value,
  output [15:0] memory_access_address,
  output write_memory,
  output [15:0] program_counter_out,
  output branch
);

  wire _4, _6, _11, _12, ADD, AND, arithmetic_1_write_flags, AShift, ashift_1_write_flags,
       branch_1_write_flags, FON_FF, fon_ff_1_write_flags, FSET, fset_1_write_flags, INC_DEC,
       inc_dec_1_write_flags, LOAD, load_1_write_flags, logic_1_write_flags, LShift, LShift8,
       lshift_1_write_flags, MUL, OR, or_1_out, or_2_out, RSTRF, rstrf_1_write_flags, SAVEF,
       savef_1_write_flags, SET, set_1_write_flags, store_1_write_flags, SUB, XOR;
  wire [3:0] _0_3, _4_7, _8_11, arithmetic_1_read_register_1, arithmetic_1_read_register_2,
       arithmetic_1_write_register, ashift_1_read_register_1, ashift_1_read_register_2,
       ashift_1_write_register, branch_1_read_register_1, branch_1_read_register_2, branch_1_write_register,
       fon_ff_1_read_register_1, fon_ff_1_read_register_2, fon_ff_1_write_register, fset_1_read_register_1,
       fset_1_read_register_2, fset_1_write_register, inc_dec_1_read_register_1, inc_dec_1_read_register_2,
       inc_dec_1_write_register, load_1_read_register_1, load_1_read_register_2, load_1_write_register,
       logic_1_read_register_1, logic_1_read_register_2, logic_1_write_register, lshift_1_read_register_1,
       lshift_1_read_register_2, lshift_1_write_register, rstrf_1_read_register_1, rstrf_1_read_register_2,
       rstrf_1_write_register, savef_1_read_register_1, savef_1_read_register_2, savef_1_write_register,
       set_1_read_register_1, set_1_read_register_2, set_1_write_register, store_1_read_register_1,
       store_1_read_register_2, store_1_write_register;
  wire [4:0] arithmetic_1_flags_out, ashift_1_flags_out, branch_1_flags_out, fon_ff_1_flags_out,
       fset_1_flags_out, inc_dec_1_flags_out, load_1_flags_out, logic_1_flags_out, lshift_1_flags_out,
       rstrf_1_flags_out, savef_1_flags_out, set_1_flag_values, store_1_flags_out;
  wire [5:0] _0_5, ARITHMETIC_flags_info, AShift_flags_info, FON_FF_flags_info, FSET_flags_info,
       INC_DEC_flags_info, LOAD_flags_info, LOGIC_flags_info, LShift_flags_info, RSTRF_flags_info,
       STORE_flags_info;
  wire [7:0] _0_7;
  wire [15:0] arithmetic_1_write_value, ashift_1_write_value, branch_1_write_value, fon_ff_1_write_value,
       fset_1_write_value, inc_dec_1_write_value, load_1_write_value, LOAD_memory_access_address,
       logic_1_write_value, lshift_1_write_value, rstrf_1_write_value, savef_1_write_value,
       set_1_write_value, store_1_write_value, STORE_memory_access_address;
  wire [31:0] ARITHMETIC_register_info, AShift_register_info, BRANCH_register_info, INC_DEC_register_info,
       LOAD_register_info, LOGIC_register_info, LShift_register_info, or_4_out, RSTRF_register_info,
       SAVEF_register_info, SET_register_info, STORE_register_info;

  op_selector op_selector_1 (
    .instruction(Instruction), .SET(SET), .AND(AND), .OR(OR), .XOR(XOR), .ADD(ADD), .SUB(SUB), .MUL(MUL),
    .LShift(LShift), .LShift8(LShift8), .AShift(AShift), .SAVEF(SAVEF), .RSTRF(RSTRF), .FON_FF(FON_FF),
    .FSET(FSET), .INC_DEC(INC_DEC), .LOAD(LOAD), .STORE(write_memory), .BRANCH(branch));
  data_splitter data_splitter_1 (
    .instruction(Instruction), ._0_3(_0_3), ._4_7(_4_7), ._8_11(_8_11), ._0_7(_0_7), ._0_5(_0_5), ._12(_12),
    ._6(_6), ._4(_4), ._11(_11));
  SET set_1 (
    .l_h(_12), .d(_8_11), .v(_0_7), .read_value(register_read_value_1), .write_flags(set_1_write_flags),
    .flag_values(set_1_flag_values), .read_register_1(set_1_read_register_1),
    .read_register_2(set_1_read_register_2), .write_register(set_1_write_register),
    .write_value(set_1_write_value));
  LOGIC logic_1 (
    .d(_8_11), .a(_4_7), .b(_0_3), .read_value_1(register_read_value_1),
    .read_value_2(register_read_value_2), .AND(AND), .OR(OR), .XOR(XOR), .flags_in(flags_in),
    .write_flags(logic_1_write_flags), .flags_out(logic_1_flags_out),
    .read_register_1(logic_1_read_register_1), .read_register_2(logic_1_read_register_2),
    .write_register(logic_1_write_register), .write_value(logic_1_write_value));
  packer packer_1 (
    .enable(SET), .write_flags(set_1_write_flags), .flags_out(set_1_flag_values),
    .read_register_1(set_1_read_register_1), .read_register_2(set_1_read_register_2),
    .write_register(set_1_write_register), .write_value(set_1_write_value), .register_info(SET_register_info));  // open: flag_info
  or or_1 (or_1_out, AND, OR, XOR);
  packer packer_2 (
    .enable(or_1_out), .write_flags(logic_1_write_flags), .flags_out(logic_1_flags_out),
    .read_register_1(logic_1_read_register_1), .read_register_2(logic_1_read_register_2),
    .write_register(logic_1_write_register), .write_value(logic_1_write_value), .flag_info(LOGIC_flags_info),
    .register_info(LOGIC_register_info));
  or or_2 (or_2_out, ADD, SUB, MUL);
  ARITHMETIC arithmetic_1 (
    .d(_8_11), .a(_4_7), .b(_0_3), .read_value_1(register_read_value_1),
    .read_value_2(register_read_value_2), .ADD(ADD), .SUB(SUB), .MUL(MUL), .flags_in(flags_in),
    .write_flags(arithmetic_1_write_flags), .flags_out(arithmetic_1_flags_out),
    .read_register_1(arithmetic_1_read_register_1), .read_register_2(arithmetic_1_read_register_2),
    .write_register(arithmetic_1_write_register), .write_value(arithmetic_1_write_value));
  packer packer_3 (
    .enable(or_2_out), .write_flags(arithmetic_1_write_flags), .flags_out(arithmetic_1_flags_out),
    .read_register_1(arithmetic_1_read_register_1), .read_register_2(arithmetic_1_read_register_2),
    .write_register(arithmetic_1_write_register), .write_value(arithmetic_1_write_value),
    .flag_info(ARITHMETIC_flags_info), .register_info(ARITHMETIC_register_info));
  LShift lshift_1 (
    .d(_8_11), .b(_0_3), .read_value(register_read_value_1), .right(_4), .flags_in(flags_in),
    .write_flags(lshift_1_write_flags), .flags_out(lshift_1_flags_out),
    .read_register_1(lshift_1_read_register_1), .read_register_2(lshift_1_read_register_2),
    .write_register(lshift_1_write_register), .write_value(lshift_1_write_value));
  packer packer_4 (
    .enable(LShift), .write_flags(lshift_1_write_flags), .flags_out(lshift_1_flags_out),
    .read_register_1(lshift_1_read_register_1), .read_register_2(lshift_1_read_register_2),
    .write_register(lshift_1_write_register), .write_value(lshift_1_write_value),
    .flag_info(LShift_flags_info), .register_info(LShift_register_info));
  AShift ashift_1 (
    .d(_8_11), .b(_0_3), .read_value(register_read_value_1), .right(_4), .flags_in(flags_in),
    .write_flags(ashift_1_write_flags), .flags_out(ashift_1_flags_out),
    .read_register_1(ashift_1_read_register_1), .read_register_2(ashift_1_read_register_2),
    .write_register(ashift_1_write_register), .write_value(ashift_1_write_value));
  packer packer_5 (
    .enable(AShift), .write_flags(ashift_1_write_flags), .flags_out(ashift_1_flags_out),
    .read_register_1(ashift_1_read_register_1), .read_register_2(ashift_1_read_register_2),
    .write_register(ashift_1_write_register), .write_value(ashift_1_write_value),
    .flag_info(AShift_flags_info), .register_info(AShift_register_info));
  SAVEF savef_1 (
    .d(_8_11), .flags_in(flags_in), .write_flags(savef_1_write_flags), .flags_out(savef_1_flags_out),
    .read_register_1(savef_1_read_register_1), .read_register_2(savef_1_read_register_2),
    .write_register(savef_1_write_register), .write_value(savef_1_write_value));
  packer packer_6 (
    .enable(SAVEF), .write_flags(savef_1_write_flags), .flags_out(savef_1_flags_out),
    .read_register_1(savef_1_read_register_1), .read_register_2(savef_1_read_register_2),
    .write_register(savef_1_write_register), .write_value(savef_1_write_value),
    .register_info(SAVEF_register_info));  // open: flag_info
  RSTRF rstrf_1 (
    .d(_8_11), .read_value(register_read_value_1), .write_flags(rstrf_1_write_flags),
    .flags_out(rstrf_1_flags_out), .read_register_1(rstrf_1_read_register_1),
    .read_register_2(rstrf_1_read_register_2), .write_register(rstrf_1_write_register),
    .write_value(rstrf_1_write_value));
  packer packer_7 (
    .enable(RSTRF), .write_flags(rstrf_1_write_flags), .flags_out(rstrf_1_flags_out),
    .read_register_1(rstrf_1_read_register_1), .read_register_2(rstrf_1_read_register_2),
    .write_register(rstrf_1_write_register), .write_value(rstrf_1_write_value), .flag_info(RSTRF_flags_info),
    .register_info(RSTRF_register_info));
  FON_FF fon_ff_1 (
    ._0_3(_0_3), ._8_11(_8_11), .flags_in(flags_in), .write_flags(fon_ff_1_write_flags),
    .flags_out(fon_ff_1_flags_out), .read_register_1(fon_ff_1_read_register_1),
    .read_register_2(fon_ff_1_read_register_2), .write_register(fon_ff_1_write_register),
    .write_value(fon_ff_1_write_value));
  packer packer_8 (
    .enable(FON_FF), .write_flags(fon_ff_1_write_flags), .flags_out(fon_ff_1_flags_out),
    .read_register_1(fon_ff_1_read_register_1), .read_register_2(fon_ff_1_read_register_2),
    .write_register(fon_ff_1_write_register), .write_value(fon_ff_1_write_value),
    .flag_info(FON_FF_flags_info));  // open: register_info
  FSET fset_1 (
    ._0_3(_0_3), ._8_11(_8_11), .flags_in(flags_in), .write_flags(fset_1_write_flags),
    .flags_out(fset_1_flags_out), .read_register_1(fset_1_read_register_1),
    .read_register_2(fset_1_read_register_2), .write_register(fset_1_write_register),
    .write_value(fset_1_write_value));
  packer packer_9 (
    .enable(FSET), .write_flags(fset_1_write_flags), .flags_out(fset_1_flags_out),
    .read_register_1(fset_1_read_register_1), .read_register_2(fset_1_read_register_2),
    .write_register(fset_1_write_register), .write_value(fset_1_write_value), .flag_info(FSET_flags_info));  // open: register_info
  INC_DEC inc_dec_1 (
    .d(_8_11), .epsilon(_0_5), .DEC(_6), .flags_in(flags_in), .register_read_value_1(register_read_value_1),
    .write_flags(inc_dec_1_write_flags), .flags_out(inc_dec_1_flags_out),
    .read_register_1(inc_dec_1_read_register_1), .read_register_2(inc_dec_1_read_register_2),
    .write_register(inc_dec_1_write_register), .write_value(inc_dec_1_write_value));
  packer packer_10 (
    .enable(INC_DEC), .write_flags(inc_dec_1_write_flags), .flags_out(inc_dec_1_flags_out),
    .read_register_1(inc_dec_1_read_register_1), .read_register_2(inc_dec_1_read_register_2),
    .write_register(inc_dec_1_write_register), .write_value(inc_dec_1_write_value),
    .flag_info(INC_DEC_flags_info), .register_info(INC_DEC_register_info));
  LOAD load_1 (
    .d(_8_11), .b(_0_3), .o({_12, _4_7}), .flags_in(flags_in), .register_read_value(register_read_value_1),
    .memory_read_value(memory_read_value), .write_flags(load_1_write_flags), .flags_out(load_1_flags_out),
    .read_register_1(load_1_read_register_1), .read_register_2(load_1_read_register_2),
    .write_register(load_1_write_register), .write_value(load_1_write_value),
    .memory_access_address(LOAD_memory_access_address));
  packer packer_11 (
    .enable(LOAD), .write_flags(load_1_write_flags), .flags_out(load_1_flags_out),
    .read_register_1(load_1_read_register_1), .read_register_2(load_1_read_register_2),
    .write_register(load_1_write_register), .write_value(load_1_write_value), .flag_info(LOAD_flags_info),
    .register_info(LOAD_register_info));
  STORE store_1 (
    .d(_8_11), .b(_0_3), .o({_12, _4_7}), .register_read_value_1(register_read_value_1),
    .register_read_value_2(register_read_value_2), .write_flags(store_1_write_flags),
    .flags_out(store_1_flags_out), .read_register_1(store_1_read_register_1),
    .read_register_2(store_1_read_register_2), .write_register(store_1_write_register),
    .write_value(store_1_write_value), .memory_access_address(STORE_memory_access_address));
  packer packer_12 (
    .enable(write_memory), .write_flags(store_1_write_flags), .flags_out(store_1_flags_out),
    .read_register_1(store_1_read_register_1), .read_register_2(store_1_read_register_2),
    .write_register(store_1_write_register), .write_value(store_1_write_value), .flag_info(STORE_flags_info),
    .register_info(STORE_register_info));
  BRANCH branch_1 (
    .ABSOLUTE(_12), .CONDITION_CODE(_8_11), .b(_0_3), .o({_4_7, _0_3}), .flags_in(flags_in),
    .program_counter_in(program_counter_in), .register_read_value(register_read_value_1),
    .write_flags(branch_1_write_flags), .flags_out(branch_1_flags_out),
    .read_register_1(branch_1_read_register_1), .read_register_2(branch_1_read_register_2),
    .write_register(branch_1_write_register), .write_value(branch_1_write_value), .PC_out(program_counter_out));
  packer packer_13 (
    .enable(branch), .write_flags(branch_1_write_flags), .flags_out(branch_1_flags_out),
    .read_register_1(branch_1_read_register_1), .read_register_2(branch_1_read_register_2),
    .write_register(branch_1_write_register), .write_value(branch_1_write_value),
    .register_info(BRANCH_register_info));  // open: flag_info
  assign {flags_out, write_flags} = LOGIC_flags_info | ARITHMETIC_flags_info | LShift_flags_info | AShift_flags_info | RSTRF_flags_info | FON_FF_flags_info | FSET_flags_info | INC_DEC_flags_info | LOAD_flags_info | STORE_flags_info;  // OR_Gate or_3, 6 bits wide
  assign or_4_out = SET_register_info | LOGIC_register_info | ARITHMETIC_register_info | LShift_register_info | AShift_register_info | SAVEF_register_info | RSTRF_register_info | INC_DEC_register_info | LOAD_register_info | STORE_register_info | BRANCH_register_info;  // OR_Gate or_4, 32 bits wide
  register_info_unpacker register_info_unpacker_1 (
    .register_info(or_4_out), .read_register_1(read_register_1), .read_register_2(read_register_2),
    .write_register(write_register), .write_value(write_value));
  Multiplexer #(.select(2), .width(16)) multiplexer_1 (
    .in1(LOAD_memory_access_address), .in2(STORE_memory_access_address), .out(memory_access_address),
    .sel({write_memory, LOAD}));  // open: in0, in3, en

  // Other names for the same wires on the sheet: STORE = write_memory; mv[15:0] = memory_read_value;
  //   PC_in[15:0] = program_counter_in; PC_out[15:0] = program_counter_out; rv1[15:0] = register_read_value_1;
  //   rv2[15:0] = register_read_value_2

  // Notes on the sheet:
  //   modules are named for their corresponding HERA command
  //   their inputs are abbreviated as in the HERA documentation
  //   hi
endmodule

module SET (
  input  l_h,
  input  [3:0] d,
  input  [7:0] v,
  input  [15:0] read_value,
  output write_flags,
  output [4:0] flag_values,
  output [3:0] read_register_1,
  output [3:0] read_register_2,
  output [3:0] write_register,
  output [15:0] write_value
);

  wire [15:0] and_1_out, and_2_out, bit_extender_1_out;

  assign bit_extender_1_out = {{15{l_h}}, l_h};  // Bit_Extender bit_extender_1
  assign and_1_out = bit_extender_1_out & {v, read_value[7:0]};  // AND_Gate and_1, 16 bits wide
  assign and_2_out = {{8{1'b0}}, v} & ~bit_extender_1_out;  // AND_Gate and_2, 16 bits wide
  assign write_value = and_1_out | and_2_out;  // OR_Gate or_1, 16 bits wide

  assign flag_values = {5{1'b0}};
  assign read_register_1 = d;
  assign read_register_2 = 4'b0000;
  assign write_flags = 1'b0;
  assign write_register = d;
endmodule

module packer (
  input  enable,
  input  write_flags,
  input  [4:0] flags_out,
  input  [3:0] read_register_1,
  input  [3:0] read_register_2,
  input  [3:0] write_register,
  input  [15:0] write_value,
  output [5:0] flag_info,
  output [31:0] register_info
);

  wire [5:0] bit_extender_1_out;
  wire [31:0] bit_extender_2_out;

  assign bit_extender_1_out = {{5{enable}}, enable};  // Bit_Extender bit_extender_1
  assign bit_extender_2_out = {{31{enable}}, enable};  // Bit_Extender bit_extender_2
  assign flag_info = bit_extender_1_out & {flags_out, write_flags};  // AND_Gate and_1, 6 bits wide
  assign register_info = bit_extender_2_out & {write_value, write_register, read_register_2, read_register_1, 4'b0000};  // AND_Gate and_2, 32 bits wide
endmodule

module register_info_unpacker (
  input  [31:0] register_info,
  output [3:0] read_register_1,
  output [3:0] read_register_2,
  output [3:0] write_register,
  output [15:0] write_value
);


  assign read_register_1 = register_info[7:4];
  assign read_register_2 = register_info[11:8];
  assign write_register = register_info[15:12];
  assign write_value = register_info[31:16];
endmodule

module op_selector (
  input  [15:0] instruction,
  output SET,
  output AND,
  output OR,
  output XOR,
  output ADD,
  output SUB,
  output MUL,
  output LShift,
  output LShift8,
  output AShift,
  output SAVEF,
  output RSTRF,
  output FON_FF,
  output FSET,
  output INC_DEC,
  output LOAD,
  output STORE,
  output BRANCH
);

  wire and_8_out, and_12_out, and_13_out, and_14_out, and_15_out, and_16_out, and_17_out, and_18_out;

  and and_1 (SET, instruction[13], instruction[14], instruction[15]);
  and and_2 (AND, ~instruction[12], ~instruction[13], ~instruction[14], instruction[15]);  // AND_Gate
  and and_3 (OR, instruction[12], ~instruction[13], ~instruction[14], instruction[15]);  // AND_Gate
  and and_4 (XOR, instruction[12], ~instruction[13], instruction[14], instruction[15]);  // AND_Gate
  and and_5 (ADD, ~instruction[12], instruction[13], ~instruction[14], instruction[15]);  // AND_Gate
  and and_6 (SUB, instruction[12], instruction[13], ~instruction[14], instruction[15]);  // AND_Gate
  and and_7 (MUL, ~instruction[12], ~instruction[13], instruction[14], instruction[15]);  // AND_Gate
  and and_8 (and_8_out, instruction[12], instruction[13], ~instruction[14], ~instruction[15]);  // AND_Gate
  and and_9 (LOAD, ~instruction[13], instruction[14], ~instruction[15]);  // AND_Gate
  and and_10 (STORE, instruction[13], instruction[14], ~instruction[15]);  // AND_Gate
  and and_11 (BRANCH, ~instruction[13], ~instruction[14], ~instruction[15]);  // AND_Gate
  and and_12 (and_12_out, ~instruction[5], ~instruction[6], ~instruction[7]);  // AND_Gate
  and and_13 (and_13_out, instruction[5], ~instruction[6], ~instruction[7]);  // AND_Gate
  and and_14 (and_14_out, ~instruction[5], instruction[6], ~instruction[7]);  // AND_Gate
  and and_15 (and_15_out, ~instruction[0], ~instruction[1], ~instruction[2], ~instruction[3], instruction[4], instruction[5], instruction[6], ~instruction[7]);  // AND_Gate
  and and_16 (and_16_out, ~instruction[0], ~instruction[1], ~instruction[2], instruction[3], instruction[4], instruction[5], instruction[6], ~instruction[7]);  // AND_Gate
  and and_17 (and_17_out, ~instruction[4], instruction[5], instruction[6], ~instruction[7], ~instruction[9], ~instruction[10]);  // AND_Gate
  and and_18 (and_18_out, ~instruction[4], instruction[5], instruction[6], ~instruction[7], ~instruction[9], instruction[10]);  // AND_Gate
  and and_19 (LShift, and_8_out, and_12_out);
  and and_20 (LShift8, and_8_out, and_13_out);
  and and_21 (AShift, and_8_out, and_14_out);
  and and_22 (SAVEF, and_8_out, and_15_out);
  and and_23 (RSTRF, and_8_out, and_16_out);
  and and_24 (FON_FF, and_8_out, and_17_out);
  and and_25 (FSET, and_8_out, and_18_out);
  and and_26 (INC_DEC, instruction[7], instruction[12], instruction[13], ~instruction[14], ~instruction[15]);  // AND_Gate
endmodule

module data_splitter (
  input  [15:0] instruction,
  output [3:0] _0_3,
  output [3:0] _4_7,
  output [3:0] _8_11,
  output [7:0] _0_7,
  output [5:0] _0_5,
  output _12,
  output _6,
  output _4,
  output _11
);


  assign _0_3 = instruction[3:0];
  assign _0_5 = instruction[5:0];
  assign _0_7 = instruction[7:0];
  assign _4 = instruction[4];
  assign _4_7 = instruction[7:4];
  assign _6 = instruction[6];
  assign _8_11 = instruction[11:8];
  assign _11 = instruction[11];
  assign _12 = instruction[12];
endmodule

module LOGIC (
  input  [3:0] d,
  input  [3:0] a,
  input  [3:0] b,
  input  [15:0] read_value_1,
  input  [15:0] read_value_2,
  input  AND,
  input  OR,
  input  XOR,
  input  [4:0] flags_in,
  output write_flags,
  output [4:0] flags_out,
  output [3:0] read_register_1,
  output [3:0] read_register_2,
  output [3:0] write_register,
  output [15:0] write_value
);

  wire [1:0] or_1_out;
  wire [15:0] and_1_out, or_3_out, xor_1_out;

  or or_1 (or_1_out[0], AND, XOR);
  or or_2 (or_1_out[1], XOR, OR);
  assign and_1_out = read_value_1 & read_value_2;  // AND_Gate and_1, 16 bits wide
  Multiplexer #(.select(2), .width(16)) multiplexer_1 (
    .in0({16{1'b0}}), .in1(and_1_out), .in2(or_3_out), .in3(xor_1_out), .out(write_value), .sel(or_1_out));  // open: en
  assign or_3_out = read_value_1 | read_value_2;  // OR_Gate or_3, 16 bits wide
  assign xor_1_out = read_value_1 ^ read_value_2;  // XOR_Gate xor_1, 16 bits wide
  zero_sign zero_sign_1 (.in_1(write_value), .zero(flags_out[1]), .sign(flags_out[0]));

  assign flags_out[4:2] = flags_in[4:2];
  assign read_register_1 = a;
  assign read_register_2 = b;
  assign write_flags = 1'b1;
  assign write_register = d;

  // Other names for the same wires on the sheet: sign_out = flags_out[0]; zero_out = flags_out[1];
  //   rv1[15:0] = read_value_1; rv2[15:0] = read_value_2
endmodule

module ARITHMETIC (
  input  [3:0] d,
  input  [3:0] a,
  input  [3:0] b,
  input  [15:0] read_value_1,
  input  [15:0] read_value_2,
  input  ADD,
  input  SUB,
  input  MUL,
  input  [4:0] flags_in,
  output write_flags,
  output [4:0] flags_out,
  output [3:0] read_register_1,
  output [3:0] read_register_2,
  output [3:0] write_register,
  output [15:0] write_value
);

  wire adder_1_cout, and_1_out, and_2_out, comparator_1_eq, not_1_out, not_2_out, subtractor_1_bout,
       xnor_1_out, xor_1_out;
  wire [1:0] OP;
  wire [15:0] adder_1_out, multiplexer_1_out, multiplier_1_cout, multiplier_1_out, negator_1_out,
       subtractor_1_out;

  or or_1 (OP[0], ADD, SUB);
  or or_2 (OP[1], SUB, MUL);
  Negator #(.width(16)) negator_1 (.in(read_value_2), .out(negator_1_out));
  Multiplexer #(.select(2), .width(16)) multiplexer_1 (
    .in0({16{1'b0}}), .in1(read_value_2), .in3(negator_1_out), .out(multiplexer_1_out), .sel(OP));  // open: in2, en
  and and_1 (and_1_out, flags_in[3], ~flags_in[4]);  // AND_Gate
  and and_2 (and_2_out, ~flags_in[4], ~flags_in[3]);  // AND_Gate
  zero_sign zero_sign_1 (.in_1(write_value), .zero(flags_out[1]), .sign(flags_out[0]));
  Adder #(.width(16)) adder_1 (
    .a(read_value_1), .b(read_value_2), .out(adder_1_out), .cin(and_1_out), .cout(adder_1_cout));
  Multiplier #(.width(16)) multiplier_1 (
    .a(read_value_1), .b(read_value_2), .out(multiplier_1_out), .cout(multiplier_1_cout));  // open: cin
  Comparator #(.width(16)) comparator_1 (.a(multiplier_1_cout), .b({16{1'b0}}), .eq(comparator_1_eq));  // open: gt, lt
  Subtractor #(.width(16)) subtractor_1 (
    .a(read_value_1), .b(read_value_2), .out(subtractor_1_out), .bin(and_2_out), .bout(subtractor_1_bout));
  xor xor_1 (xor_1_out, write_value[15], multiplexer_1_out[15]);
  xnor xnor_1 (xnor_1_out, multiplexer_1_out[15], read_value_1[15]);
  Multiplexer #(.select(2), .width(16)) multiplexer_2 (
    .in0({16{1'b0}}), .in1(adder_1_out), .in2(multiplier_1_out), .in3(subtractor_1_out), .out(write_value),
    .sel(OP));  // open: en
  not not_1 (not_1_out, comparator_1_eq);
  not not_2 (not_2_out, subtractor_1_bout);
  and and_3 (flags_out[2], xor_1_out, xnor_1_out);
  Multiplexer #(.select(2)) multiplexer_3 (
    .in0(1'b0), .in1(adder_1_cout), .in2(not_1_out), .in3(not_2_out), .out(flags_out[3]), .sel(OP));  // open: en

  assign flags_out[4] = flags_in[4];
  assign read_register_1 = a;
  assign read_register_2 = b;
  assign write_flags = 1'b1;
  assign write_register = d;

  // Other names for the same wires on the sheet: overflow_in = flags_in[2]; carry_in = flags_in[3];
  //   carry_block_in = flags_in[4]; sign_out = flags_out[0]; zero_out = flags_out[1]; overflow_out = flags_out[2];
  //   carry_out = flags_out[3]; rv1[15:0] = read_value_1; rv2[15:0] = read_value_2
endmodule

module zero_sign (
  input  [15:0] in_1,
  output zero,
  output sign
);

  nor nor_1 (zero, in_1[0], in_1[1], in_1[2], in_1[3], in_1[4], in_1[5], in_1[6], in_1[7], in_1[9], in_1[10], in_1[11], in_1[12], in_1[13], in_1[14], in_1[15], in_1[8]);

  assign sign = in_1[15];
endmodule

module LShift (
  input  [3:0] d,
  input  [3:0] b,
  input  [15:0] read_value,
  input  right,
  input  [4:0] flags_in,
  output write_flags,
  output [4:0] flags_out,
  output [3:0] read_register_1,
  output [3:0] read_register_2,
  output [3:0] write_register,
  output [15:0] write_value
);

  wire [0:0] and_1_out;

  and and_1 (and_1_out[0], flags_in[3], ~flags_in[4]);  // AND_Gate
  Multiplexer #(.width(16)) multiplexer_1 (
    .in0({read_value[14:0], and_1_out[0]}), .in1({and_1_out[0], read_value[15:1]}), .out(write_value),
    .sel(right));  // open: en
  Multiplexer multiplexer_2 (.in0(read_value[15]), .in1(read_value[0]), .out(flags_out[3]), .sel(right));  // open: en
  zero_sign zero_sign_1 (.in_1(write_value), .zero(flags_out[1]), .sign(flags_out[0]));

  assign {flags_out[4], flags_out[2]} = {flags_in[4], flags_in[2]};
  assign read_register_1 = b;
  assign read_register_2 = 4'b0000;
  assign write_flags = 1'b1;
  assign write_register = d;

  // Other names for the same wires on the sheet: rv[15:0] = read_value; carry_in = flags_in[3];
  //   sign_out = flags_out[0]; zero_out = flags_out[1]; overflow_in = flags_in[2]; carry_out = flags_out[3];
  //   carry_block_in = flags_in[4]
endmodule

module AShift (
  input  [3:0] d,
  input  [3:0] b,
  input  [15:0] read_value,
  input  right,
  input  [4:0] flags_in,
  output write_flags,
  output [4:0] flags_out,
  output [3:0] read_register_1,
  output [3:0] read_register_2,
  output [3:0] write_register,
  output [15:0] write_value
);

  wire xor_1_out;
  wire [0:0] and_1_out;

  and and_1 (and_1_out[0], flags_in[3], ~flags_in[4]);  // AND_Gate
  Multiplexer #(.width(16)) multiplexer_1 (
    .in0({read_value[14:0], and_1_out[0]}), .in1({{2{read_value[15]}}, read_value[14:1]}), .out(write_value),
    .sel(right));  // open: en
  Multiplexer multiplexer_2 (.in0(read_value[15]), .in1(read_value[0]), .out(flags_out[3]), .sel(right));  // open: en
  zero_sign zero_sign_1 (.in_1(write_value), .zero(flags_out[1]), .sign(flags_out[0]));
  xor xor_1 (xor_1_out, flags_out[0], read_value[15]);
  Multiplexer multiplexer_3 (.in0(xor_1_out), .in1(flags_in[2]), .out(flags_out[2]), .sel(right));  // open: en

  assign flags_out[4] = flags_in[4];
  assign read_register_1 = b;
  assign read_register_2 = 4'b0000;
  assign write_flags = 1'b1;
  assign write_register = d;

  // Other names for the same wires on the sheet: rv[15:0] = read_value; carry_in = flags_in[3];
  //   sign_out = flags_out[0]; zero_out = flags_out[1]; overflow_out = flags_out[2]; carry_out = flags_out[3];
  //   carry_block_in = flags_in[4]
endmodule

module SAVEF (
  input  [3:0] d,
  input  [4:0] flags_in,
  output write_flags,
  output [4:0] flags_out,
  output [3:0] read_register_1,
  output [3:0] read_register_2,
  output [3:0] write_register,
  output [15:0] write_value
);


  assign flags_out = {5{1'b0}};
  assign read_register_1 = 4'b0000;
  assign read_register_2 = 4'b0000;
  assign write_flags = 1'b0;
  assign write_register = d;
  assign write_value = {{11{1'b0}}, flags_in};
endmodule

module RSTRF (
  input  [3:0] d,
  input  [15:0] read_value,
  output write_flags,
  output [4:0] flags_out,
  output [3:0] read_register_1,
  output [3:0] read_register_2,
  output [3:0] write_register,
  output [15:0] write_value
);


  assign flags_out = read_value[4:0];
  assign read_register_1 = d;
  assign read_register_2 = 4'b0000;
  assign write_flags = 1'b1;
  assign write_register = 4'b0000;
  assign write_value = {16{1'b0}};
endmodule

module FON_FF (
  input  [3:0] _0_3,
  input  [3:0] _8_11,
  input  [4:0] flags_in,
  output write_flags,
  output [4:0] flags_out,
  output [3:0] read_register_1,
  output [3:0] read_register_2,
  output [3:0] write_register,
  output [15:0] write_value
);

  wire not_1_out;

  not not_1 (not_1_out, _8_11[3]);
  Multiplexer multiplexer_1 (.in0(flags_in[0]), .in1(not_1_out), .out(flags_out[0]), .sel(_0_3[0]));  // open: en
  Multiplexer multiplexer_2 (.in0(flags_in[1]), .in1(not_1_out), .out(flags_out[1]), .sel(_0_3[1]));  // open: en
  Multiplexer multiplexer_3 (.in0(flags_in[2]), .in1(not_1_out), .out(flags_out[2]), .sel(_0_3[2]));  // open: en
  Multiplexer multiplexer_4 (.in0(flags_in[3]), .in1(not_1_out), .out(flags_out[3]), .sel(_0_3[3]));  // open: en
  Multiplexer multiplexer_5 (.in0(flags_in[4]), .in1(not_1_out), .out(flags_out[4]), .sel(_8_11[0]));  // open: en

  assign read_register_1 = 4'b0000;
  assign read_register_2 = 4'b0000;
  assign write_flags = 1'b1;
  assign write_register = 4'b0000;
  assign write_value = {16{1'b0}};
endmodule

module FSET (
  input  [3:0] _0_3,
  input  [3:0] _8_11,
  input  [4:0] flags_in,
  output write_flags,
  output [4:0] flags_out,
  output [3:0] read_register_1,
  output [3:0] read_register_2,
  output [3:0] write_register,
  output [15:0] write_value
);

  Multiplexer multiplexer_1 (.in0(_8_11[0]), .in1(flags_in[4]), .out(flags_out[4]), .sel(_8_11[3]));  // open: en

  assign flags_out[3:0] = _0_3;
  assign read_register_1 = 4'b0000;
  assign read_register_2 = 4'b0000;
  assign write_flags = 1'b1;
  assign write_register = 4'b0000;
  assign write_value = {16{1'b0}};
endmodule

module LOAD (
  input  [3:0] d,
  input  [3:0] b,
  input  [4:0] o,
  input  [4:0] flags_in,
  input  [15:0] register_read_value,
  input  [15:0] memory_read_value,
  output write_flags,
  output [4:0] flags_out,
  output [3:0] read_register_1,
  output [3:0] read_register_2,
  output [3:0] write_register,
  output [15:0] write_value,
  output [15:0] memory_access_address
);

  zero_sign zero_sign_1 (.in_1(memory_read_value), .zero(flags_out[1]), .sign(flags_out[0]));
  Adder #(.width(16)) adder_1 (
    .a({{11{1'b0}}, o}), .b(register_read_value), .out(memory_access_address));  // open: cin, cout

  assign flags_out[4:2] = flags_in[4:2];
  assign read_register_1 = b;
  assign read_register_2 = 4'b0000;
  assign write_flags = 1'b1;
  assign write_register = d;
  assign write_value = memory_read_value;

  // Other names for the same wires on the sheet: sign_out = flags_out[0]; zero_out = flags_out[1]
endmodule

module STORE (
  input  [3:0] d,
  input  [3:0] b,
  input  [4:0] o,
  input  [15:0] register_read_value_1,
  input  [15:0] register_read_value_2,
  output write_flags,
  output [4:0] flags_out,
  output [3:0] read_register_1,
  output [3:0] read_register_2,
  output [3:0] write_register,
  output [15:0] write_value,
  output [15:0] memory_access_address
);

  Adder #(.width(16)) adder_1 (
    .a({{11{1'b0}}, o}), .b(register_read_value_2), .out(memory_access_address));  // open: cin, cout

  assign flags_out = {5{1'b0}};
  assign read_register_1 = d;
  assign read_register_2 = b;
  assign write_flags = 1'b0;
  assign write_register = 4'b0000;
  assign write_value = register_read_value_1;
endmodule

module INC_DEC (
  input  [3:0] d,
  input  [5:0] epsilon,
  input  DEC,
  input  [4:0] flags_in,
  input  [15:0] register_read_value_1,
  output write_flags,
  output [4:0] flags_out,
  output [3:0] read_register_1,
  output [3:0] read_register_2,
  output [3:0] write_register,
  output [15:0] write_value
);

  wire adder_1_cout, not_1_out, subtractor_1_bout;
  wire [15:0] adder_1_out, subtractor_1_out;

  Adder #(.width(16)) adder_1 (
    .a({{10{1'b0}}, epsilon}), .b(register_read_value_1), .out(adder_1_out), .cin(1'b1), .cout(adder_1_cout));
  Multiplexer #(.width(16)) multiplexer_1 (
    .in0(adder_1_out), .in1(subtractor_1_out), .out(write_value), .sel(DEC));  // open: en
  Subtractor #(.width(16)) subtractor_1 (
    .a({{10{1'b0}}, epsilon}), .b(register_read_value_1), .out(subtractor_1_out), .bin(1'b1),
    .bout(subtractor_1_bout));
  Multiplexer multiplexer_2 (.in0(adder_1_cout), .in1(not_1_out), .out(flags_out[3]), .sel(DEC));  // open: en
  not not_1 (not_1_out, subtractor_1_bout);
  zero_sign zero_sign_1 (.in_1(write_value), .zero(flags_out[1]), .sign(flags_out[0]));
  xor xor_1 (flags_out[2], write_value[15], register_read_value_1[15]);

  assign flags_out[4] = flags_in[4];
  assign read_register_1 = d;
  assign read_register_2 = 4'b0000;
  assign write_flags = 1'b1;
  assign write_register = d;

  // Other names for the same wires on the sheet: sign_out = flags_out[0]; zero_out = flags_out[1];
  //   overflow_out = flags_out[2]; carry_out = flags_out[3]; carry_block_in = flags_in[4]
endmodule

module BRANCH (
  input  ABSOLUTE,
  input  [3:0] CONDITION_CODE,
  input  [3:0] b,
  input  [7:0] o,
  input  [4:0] flags_in,
  input  [15:0] program_counter_in,
  input  [15:0] register_read_value,
  output write_flags,
  output [4:0] flags_out,
  output [3:0] read_register_1,
  output [3:0] read_register_2,
  output [3:0] write_register,
  output [15:0] write_value,
  output [15:0] PC_out
);

  wire BL_BGE_out, BLE_BG_out, BULE_BUG_out, multiplexer_1_out, not_1_out, not_2_out, not_3_out, not_4_out,
       not_5_out, not_6_out, not_7_out, xor_1_out;
  wire [15:0] adder_1_out, multiplexer_2_out;

  xor BL_BGE (BL_BGE_out, flags_in[0], flags_in[2]);
  xor xor_1 (xor_1_out, flags_in[0], flags_in[2]);
  or BLE_BG (BLE_BG_out, xor_1_out, flags_in[1]);
  or BULE_BUG (BULE_BUG_out, ~flags_in[3], flags_in[1]);  // OR_Gate
  not not_1 (not_1_out, BL_BGE_out);
  not not_2 (not_2_out, BLE_BG_out);
  not not_3 (not_3_out, BULE_BUG_out);
  Multiplexer #(.select(4)) multiplexer_1 (
    .in0(1'b1), .in1(1'b0), .in2(BL_BGE_out), .in3(not_1_out), .in4(BLE_BG_out), .in5(not_2_out),
    .in6(BULE_BUG_out), .in7(not_3_out), .in8(flags_in[1]), .in9(not_4_out), .in10(flags_in[3]),
    .in11(not_5_out), .in12(flags_in[0]), .in13(not_6_out), .in14(flags_in[2]), .in15(not_7_out),
    .out(multiplexer_1_out), .sel(CONDITION_CODE));  // open: en
  not not_4 (not_4_out, flags_in[1]);
  not not_5 (not_5_out, flags_in[3]);
  not not_6 (not_6_out, flags_in[0]);
  not not_7 (not_7_out, flags_in[2]);
  Adder #(.width(16)) adder_1 (.a(program_counter_in), .b({{9{o[7]}}, o[6:0]}), .out(adder_1_out));  // open: cin, cout
  Multiplexer #(.width(16)) multiplexer_2 (
    .in0(adder_1_out), .in1(register_read_value), .out(multiplexer_2_out), .sel(ABSOLUTE));  // open: en
  Multiplexer #(.width(16)) multiplexer_3 (
    .in0(program_counter_in), .in1(multiplexer_2_out), .out(PC_out), .sel(multiplexer_1_out));  // open: en

  assign flags_out = {5{1'b0}};
  assign read_register_1 = b;
  assign read_register_2 = 4'b0000;
  assign write_flags = 1'b0;
  assign write_register = 4'b0000;
  assign write_value = {16{1'b0}};

  // Other names for the same wires on the sheet: ABS = ABSOLUTE; CC[3:0] = CONDITION_CODE; sign_in = flags_in[0];
  //   zero_in = flags_in[1]; overflow_in = flags_in[2]; carry_in = flags_in[3]; carry_block_in = flags_in[4];
  //   PC_in[15:0] = program_counter_in
endmodule
